# Fritzing sketch diagrama (saved by Fritzing 0.9.3b)
breadboards: 1

parts:
  Componente1 = Arduino Uno (Rev3)
  Componente2 = Bluetooth HC-05 Macho  # not connected
  J1 = Basic Servo

nets:
  N1: Componente1.D7, J1.pulse
  GND: Componente1.GND, J1.gnd
  VIN: Componente1.VIN, J1.vcc
